# Fritzing sketch GarageDoorOpener (saved by Fritzing 0.9.3b)
breadboards: 1

parts:
  Raspberry_Pi_Zero_WH = Raspberry Pi Zero
  2_Channel_Relay_Module = 2 Channel Power Relay
  5v_DC_adapter = Power plug
  CLOSE_(NO)_Pushbutton = Round Pushbutton
  OPEN_(NO)_Pushbutton = Round Pushbutton
  R1 = Resistor [tolerance=±5% resistance=10k package="2010 [SMD]"]
  resistor = Resistor [tolerance=±5% resistance=10k package="2010 [SMD]"]
  resistor_2 = Resistor [tolerance=±5% resistance=1k package="2010 [SMD]"]
  resistor_3 = Resistor [tolerance=±5% resistance=1k package="2010 [SMD]"]
  AC240v_GARAGE_MOTOR_(UP/DOWN) = AC240vMotor - Bipolar
  AC240v_Source = Power plug

nets:
  N1: Raspberry_Pi_Zero_WH.pin_1, Raspberry_Pi_Zero_WH.pin_17, 2_Channel_Relay_Module.VCC
  N2: Raspberry_Pi_Zero_WH.pin_6, Raspberry_Pi_Zero_WH.pin_8, Raspberry_Pi_Zero_WH.pin_9, Raspberry_Pi_Zero_WH.pin_12, Raspberry_Pi_Zero_WH.pin_14, Raspberry_Pi_Zero_WH.pin_15, Raspberry_Pi_Zero_WH.pin_16, Raspberry_Pi_Zero_WH.pin_20, Raspberry_Pi_Zero_WH.pin_22, Raspberry_Pi_Zero_WH.pin_24, Raspberry_Pi_Zero_WH.pin_25, Raspberry_Pi_Zero_WH.pin_26, Raspberry_Pi_Zero_WH.pin_27, Raspberry_Pi_Zero_WH.pin_29, Raspberry_Pi_Zero_WH.pin_39, 2_Channel_Relay_Module.IN2, CLOSE_(NO)_Pushbutton.leg0, OPEN_(NO)_Pushbutton.leg0, resistor_2.Pin_1
  N3: Raspberry_Pi_Zero_WH.pin_13, 2_Channel_Relay_Module.IN1
  N4: Raspberry_Pi_Zero_WH.pin_31, resistor_3.Pin_1
  N5: 2_Channel_Relay_Module.JD-VCC, 5v_DC_adapter.VCC
  GND: 2_Channel_Relay_Module.GND, 5v_DC_adapter.GND
  N6: 2_Channel_Relay_Module.K1-NO, AC240v_GARAGE_MOTOR_(UP/DOWN).Phase_(UP)
  N7: 2_Channel_Relay_Module.K2-NO, AC240v_GARAGE_MOTOR_(UP/DOWN).Phase_(DOWN)
  N8: CLOSE_(NO)_Pushbutton.leg1, R1.Pin_0, resistor_2.Pin_0
  N9: OPEN_(NO)_Pushbutton.leg1, resistor.Pin_0, resistor_3.Pin_0
  N10: R1.Pin_1, resistor.Pin_1
  N11: AC240v_GARAGE_MOTOR_(UP/DOWN).Neutral, AC240v_Source.VCC

notes:
  EARTH/GROUND
  PHASE
  NEUTRAL
  PHASE (UP)
  PHASE (DOWN)
  IN1 (down signal)
  Vcc
  IN2 (up signal)
  +         JDVcc
  COMM1
  COMM2
  NO2
  NO1
  -          Gnd
  to GND gpio pin 6
  to 3.3v gpio pin 1
  to gpio pin 31 (BCM6)
  to gpio pin 29 (BCM5)
  3.3V gpio pin 17
  to gpio pin 15
  (BCM22)
  to gpio pin 13
  (BCM27)

custom parts:
  2 Channel Power Relay: A 2 channel power relay. The module operates at 5V.
  AC240vMotor - Bipolar: 4 wire up/down direction AC motor
